// Logisim project Circuito_Projeto_Final.circ as structural Verilog: 2 circuits, main circuit main
module main (
  input  [3:0] ALU_OP
);

  wire ADDIU_out, ALU_SRC, ANDI_out, CLK, LOAD, LW_out, REG_DEST, REG_W, registerfile_1_p7, STORE;
  wire [4:0] multiplexer_1_out;
  wire [31:0] adder_1_out, bit_extender_1_out, mips_alu_1_p4, mips_ram_1_p4, mipsprogramrom_1_p2,
       multiplexer_2_out, register_1_q, registerfile_1_p1, registerfile_1_p8;

  Adder #(.width(32)) adder_1 (.a(register_1_q), .b(32'h4), .out(adder_1_out));  // open: cin, cout
  Register #(.width(32)) register_1 (.D(adder_1_out), .clk(CLK), .Q(register_1_q));  // open: en, clr
  Clock u_CLK (.out(CLK));
  // MIPSProgramROM mipsprogramrom_1: pin names not known; wires that end beside it: register_1_q, mipsprogramrom_1_p2
  Multiplexer #(.width(5), .enable("false")) multiplexer_1 (
    .in0(mipsprogramrom_1_p2[15:11]), .in1(mipsprogramrom_1_p2[20:16]), .out(multiplexer_1_out),
    .sel(REG_DEST));
  and ADDIU (ADDIU_out, mipsprogramrom_1_p2[26], ~mipsprogramrom_1_p2[27], ~mipsprogramrom_1_p2[28], mipsprogramrom_1_p2[29], ~mipsprogramrom_1_p2[30], ~mipsprogramrom_1_p2[31]);  // AND_Gate
  // AND_Gate SW has open pins: in0=mipsprogramrom_1_p2[26], in1=mipsprogramrom_1_p2[27], in2=mipsprogramrom_1_p2[28], in3=mipsprogramrom_1_p2[29], in4=mipsprogramrom_1_p2[30], in5=mipsprogramrom_1_p2[31], out=open
  and LW (LW_out, mipsprogramrom_1_p2[26], mipsprogramrom_1_p2[27], ~mipsprogramrom_1_p2[28], ~mipsprogramrom_1_p2[29], ~mipsprogramrom_1_p2[30], mipsprogramrom_1_p2[31]);  // AND_Gate
  and ANDI (ANDI_out, ~mipsprogramrom_1_p2[26], ~mipsprogramrom_1_p2[27], mipsprogramrom_1_p2[28], mipsprogramrom_1_p2[29], ~mipsprogramrom_1_p2[30], ~mipsprogramrom_1_p2[31]);  // AND_Gate
  assign bit_extender_1_out = {{16{mipsprogramrom_1_p2[15]}}, mipsprogramrom_1_p2[15:0]};  // Bit_Extender bit_extender_1
  // RegisterFile registerfile_1: pin names not known; wires that end beside it: registerfile_1_p1, CLK, REG_W, multiplexer_1_out, mipsprogramrom_1_p2[25:21], mipsprogramrom_1_p2[20:16], registerfile_1_p7, registerfile_1_p8
  or or_1 (REG_DEST, ADDIU_out, LW_out, ANDI_out, ANDI_out);
  or or_2 (ALU_SRC, ADDIU_out, LW_out, ANDI_out, ANDI_out);
  or or_3 (REG_W, ADDIU_out, ANDI_out, ANDI_out);
  and and_1 (STORE, ANDI_out, ~LW_out);  // AND_Gate
  and and_2 (LOAD, LW_out, ~ANDI_out);  // AND_Gate
  Multiplexer #(.width(32), .enable("false")) multiplexer_2 (
    .in0(registerfile_1_p8), .in1(bit_extender_1_out), .out(multiplexer_2_out), .sel(ALU_SRC));
  // Mips_ALU mips_alu_1: pin names not known; wires that end beside it: registerfile_1_p7, multiplexer_2_out, ALU_OP, mips_alu_1_p4, mips_alu_1_p4[19:0], registerfile_1_p8
  // MIPS_RAM mips_ram_1: pin names not known; wires that end beside it: STORE, CLK, LOAD, mips_ram_1_p4
  Multiplexer #(.width(32), .enable("false")) multiplexer_3 (
    .in0(mips_alu_1_p4), .in1(mips_ram_1_p4), .out(registerfile_1_p1), .sel(LOAD));

  // Other names for the same wires on the sheet: MEM_TO_REG = LOAD

  // Notes on the sheet:
  //   contents of mipsprogramrom_1 (hex, n*v repeats v):
  //   addiu $1, $1, 0x26 addiu $1, $1, 0x4C addiu $1, $1, 0x4C  andi $2, $1, 0xFF  sw $2, 0($3)
  //   r
  //   i
endmodule

module control (
  input  [5:0] in_1,
  output REG_DEST,
  output ALU_SRC,
  output REG_W,
  output St,
  output Ld,
  output MEM_TO_REG
);

  wire ADDIU_out, ANDI_out, LOAD_out;

  and ADDIU (ADDIU_out, in_1[0], ~in_1[1], ~in_1[2], in_1[3], ~in_1[4], ~in_1[5]);  // AND_Gate
  // AND_Gate STORE has open pins: in0=in_1[0], in1=in_1[1], in2=in_1[2], in3=in_1[3], in4=in_1[4], in5=in_1[5], out=open
  and LOAD (LOAD_out, in_1[0], in_1[1], ~in_1[2], ~in_1[3], ~in_1[4], in_1[5]);  // AND_Gate
  and ANDI (ANDI_out, ~in_1[0], ~in_1[1], in_1[2], in_1[3], ~in_1[4], ~in_1[5]);  // AND_Gate
  or or_1 (REG_DEST, ADDIU_out, LOAD_out, ANDI_out, ANDI_out);
  or or_2 (ALU_SRC, ADDIU_out, LOAD_out, ANDI_out, ANDI_out);
  or or_3 (REG_W, ADDIU_out, ANDI_out, ANDI_out);
  and and_1 (St, ANDI_out, ~LOAD_out);  // AND_Gate
  and and_2 (Ld, LOAD_out, ~ANDI_out);  // AND_Gate

  assign MEM_TO_REG = Ld;
endmodule
